# Fritzing sketch traffic-light (saved by Fritzing 0.9.3b)
breadboards: 1

parts:
  R1 = Resistor [tolerance=±5% resistance=220 package=THT]
  R3 = Resistor [tolerance=±5% resistance=220 package=THT]
  LED1 = LED - 5mm [color="Red (633nm)" package="5 mm [THT]"]
  LED2 = LED - 5mm [color="Yellow (595nm)" package="5 mm [THT]"]
  LED3 = LED - 5mm [color="Green (570nm)" package="5 mm [THT]"]
  R4 = Resistor [tolerance=±5% resistance=220 package=THT]
  Part1 = Arduino Mega 2560 (Rev3)
  ZS-042_RTC1 = ZS-042 RTC Module

nets:
  N1: R1.Pin_0, Part1.D22
  N2: R1.Pin_1, LED3.anode
  N3: R3.Pin_0, Part1.D24
  N4: R3.Pin_1, LED1.anode
  GND: LED1.cathode, LED2.cathode, LED3.cathode, Part1.GND, ZS-042_RTC1.GND
  N5: LED2.anode, R4.Pin_1
  N6: R4.Pin_0, Part1.D23
  N7: Part1.D21/SCL, ZS-042_RTC1.SCL
  N8: Part1.D20/SDA, ZS-042_RTC1.SDA
